// Logisim project CPU.circ as structural Verilog
module CPU__RC8B1 (
  input  [7:0] IO_data_in,
  input  IO_clock_in,
  output [7:0] IO_data_out,
  output IO_clock_out
);

  wire A_read, A_write, ALU_enable, ALU_mode, and_1_out, B_read, B_write, C_read, C_write, CLOCK,
       clock_1_out, cu_1_clockhandeler_stop, enableToBus, instruction_register_write, IO_addToArray,
       IO_getLength, IO_nextByte, IO_readByte, IO_send, IO_toBus, or_1_out, PC_disable, PC_inc, PC_set,
       RAM_read, RAM_write, RESET;
  wire [3:0] ALU_flags;
  wire [7:0] A_qurrent, B_qurrent, BUS, C_qurrent, command, instruction_splitter_1_command, IO_length,
       IO_out, \parameter , PC_adr, PC_value, RAM_adress, ROM_adress, toBus;
  wire [15:0] BUS__RAMformat, RAM_data__in, RAM_data__out, ROM_data;

  // Probe on BUS
  // Probe on BUS__RAMformat
  // Probe on ALU_flags
  // Probe on RAM_data__out
  // Probe on command
  // Probe on \parameter 
  // Probe on PC_value
  // Probe on IO_out
  // Probe on IO_length
  Clock clock_1 (.out(clock_1_out));
  CU cu_1 (
    .CLOCK(CLOCK), .RESET(RESET), .ROM_data(ROM_data), .command(command), .\parameter (\parameter ),
    .BUS__RAMformat(BUS__RAMformat), .BUS(BUS), .ALU_flags(ALU_flags), .PC_value(PC_value),
    .IO_length(IO_length), .A_read(A_read), .A_write(A_write), .B_read(B_read), .B_write(B_write),
    .C_read(C_read), .C_write(C_write), .ALU_mode(ALU_mode), .ALU_enable(ALU_enable), .RAM_read(RAM_read),
    .RAM_write(RAM_write), .RAM_adress(RAM_adress), .ROM_adress(ROM_adress), .RAM_data__in(RAM_data__in),
    .instruction_register_write(instruction_register_write), .PC_inc(PC_inc), .PC_set(PC_set),
    .PC_adr(PC_adr), .IO_nextByte(IO_nextByte), .IO_readbyte(IO_readByte), .IO_send(IO_send),
    .IO_addToArray(IO_addToArray), .IO_toBus(IO_toBus), .IO_getLength(IO_getLength), .toBus(toBus),
    .enableToBus(enableToBus), .clockhandeler_stop(cu_1_clockhandeler_stop), .ROM_length(8'h14),
    .PC_disable(PC_disable));
  clock_handeler clock_handeler_1 (
    .clock_in(clock_1_out), .stop(cu_1_clockhandeler_stop), .start(RESET), .clock_out(CLOCK));
  Button button_1 (.out(RESET));
  ROM #(.dataWidth(16)) rom_1 (.addr(ROM_adress), .data(ROM_data), .sel(1'b1));
  Transistor #(.\type ("n"), .width(8)) transistor_1 (.in(toBus), .out(BUS), .gate(enableToBus));
  instruction_splitter instruction_splitter_1 (
    .raw(RAM_data__out), .command(instruction_splitter_1_command));  // open: parameter
  inst_RAM RAM (
    .save(RAM_write), .load(RAM_read), .adr(RAM_adress), .data__in(RAM_data__in), .clock(CLOCK),
    .RESET(RESET), .data__out(RAM_data__out));
  insruction_register IR (
    .set(instruction_register_write), .raw_line(RAM_data__out), .RESET(RESET), .CLOCK(CLOCK),
    .command(command), .\parameter (\parameter ));
  PC PC (.inc(PC_inc), .jump(PC_set), .adr(PC_adr), .clock(and_1_out), .RESET(or_1_out), .qurrent(PC_value));
  and and_1 (and_1_out, CLOCK, ~PC_disable);  // AND_Gate
  or or_1 (or_1_out, PC_disable, RESET);
  // Probe on BUS
  Transistor #(.\type ("n"), .width(8)) transistor_2 (.in(instruction_splitter_1_command), .out(BUS), .gate(RAM_read));
  Transistor #(.\type ("n"), .gate("br"), .width(8)) transistor_3 (.in(IO_length), .out(BUS), .gate(IO_readByte));
  Transistor #(.\type ("n"), .gate("br"), .width(8)) transistor_4 (.in(IO_length), .out(BUS), .gate(IO_getLength));
  data_register A (
    .write(A_write), .data__in(BUS), .read(A_read), .RESET(RESET), .CLOCK(CLOCK), .qurrent(A_qurrent),
    .data__out(BUS));
  data_register B (
    .write(B_write), .data__in(BUS), .read(B_read), .RESET(RESET), .CLOCK(CLOCK), .qurrent(B_qurrent),
    .data__out(BUS));
  ALU ALU (
    .A(A_qurrent), .B(B_qurrent), .adder_mode(ALU_mode), .enable(ALU_enable), .math_out(BUS),
    .flags_out(ALU_flags));
  data_register C (
    .write(C_write), .data__in(BUS), .read(C_read), .RESET(RESET), .CLOCK(CLOCK), .qurrent(C_qurrent),
    .data__out(BUS));
  // Probe on C_qurrent
  instruction_combiner instruction_combiner_1 (.command(BUS), .combined(BUS__RAMformat));  // open: parameter
  Pull_Resistor pull_resistor_1 (.node(IO_data_out));
  Pull_Resistor pull_resistor_2 (.node(IO_clock_out));
  IO_module io_module_1 (
    .nextByte(IO_nextByte), .readByte(IO_readByte), .send(IO_send), .addToArray(IO_addToArray),
    .byteIn(C_qurrent), .data_out(IO_data_out), .clock_out(IO_clock_out), .data_in(IO_data_in),
    .clock_in(IO_clock_in), .CLOCK(CLOCK), .RESET(RESET), .out(IO_out), .length(IO_length));  // open: CLEAR

  // Notes on the sheet:
  //   IO_data_out: pull=down
  //   IO_clock_out: pull=down
  //   IO_clock_in: pull=down
  //   IO_data_in: pull=down
  //   contents of rom_1 (hex, n*v repeats v):
  //   f0d 1 0 a01 700 500 f04 a01 700 300 600 f08 b 90c a01 800 500 1720 160f 800 1b00
endmodule

module CU (
  input  CLOCK,
  input  RESET,
  input  [15:0] ROM_data,
  input  [7:0] command,
  input  [7:0] \parameter ,
  input  [15:0] BUS__RAMformat,
  input  [7:0] BUS,
  input  [3:0] ALU_flags,
  input  [7:0] PC_value,
  input  [7:0] IO_length,
  input  [7:0] ROM_length,
  output A_read,
  output A_write,
  output B_read,
  output B_write,
  output C_read,
  output C_write,
  output ALU_mode,
  output ALU_enable,
  output RAM_read,
  output RAM_write,
  output [7:0] RAM_adress,
  output [7:0] ROM_adress,
  output [15:0] RAM_data__in,
  output instruction_register_write,
  output PC_inc,
  output PC_set,
  output [7:0] PC_adr,
  output IO_nextByte,
  output IO_readbyte,
  output IO_send,
  output IO_addToArray,
  output IO_toBus,
  output IO_getLength,
  output [7:0] toBus,
  output enableToBus,
  output clockhandeler_stop,
  output PC_disable
);

  wire A_to_B, A_to_C, A_to_RAM, add, and_2_out, and_3_out, and_32_out, and_33_out, and_34_out, and_35_out,
       and_36_out, and_37_out, and_38_out, anybit_1_out_2, B_to_A, B_to_C, B_to_RAM, C_to_A, C_to_B,
       C_to_RAM, comparator_1_gt, CToIfState, equals_1_out_3, equals_2_out_3, equals_3_out_3, equals_4_out_3,
       equals_5_out_3, equals_6_out_3, equals_7_out_3, equals_8_out_3, equals_9_out_3, equals_10_out_3,
       equals_11_out_3, equals_12_out_3, equals_13_out_3, equals_14_out_3, equals_15_out_3, equals_16_out_3,
       equals_17_out_3, equals_18_out_3, equals_19_out_3, equals_20_out_3, equals_21_out_3, equals_22_out_3,
       equals_23_out_3, equals_24_out_3, equals_25_out_3, equals_26_out_3, equals_27_out_3,
       f_flipflop_1_qurrent, flag_comparer_1_out, if_result_q, ifAvailable, ifFlags, inst_loader_1_done,
       inst_loader_1_trigger, jump, jumpIf, jumpIfNot, not_2_out, not_3_out, or_1_out, or_2_out, or_3_out,
       or_5_out, or_6_out, or_7_out, or_8_out, or_9_out, or_10_out, or_16_out, or_17_out, or_18_out,
       or_19_out, or_23_out, or_25_out, or_26_out, pulse_gen_1_pulse, RAM_to_A, RAM_to_B, RAM_to_C,
       s_r_latch_1_qurrent;
  wire [7:0] pull_resistor_2_node, transistor_1_out, transistor_4_out;

  Transistor #(.\type ("n"), .width(8)) transistor_1 (.in(ROM_adress), .out(transistor_1_out), .gate(PC_disable));
  inst_loader inst_loader_1 (
    .start(pulse_gen_1_pulse), .ROM_length(ROM_length), .clock(CLOCK), .RESET(RESET),
    .trigger(inst_loader_1_trigger), .i(ROM_adress), .done(inst_loader_1_done));
  not not_1 (PC_disable, inst_loader_1_done);
  Transistor #(.\type ("n"), .width(16)) transistor_2 (.in(ROM_data), .out(RAM_data__in), .gate(PC_disable));
  Transistor #(.width(16)) transistor_3 (.in(BUS__RAMformat), .out(RAM_data__in), .gate(PC_disable));
  pulse_gen pulse_gen_1 (.trigger(not_2_out), .pulse(pulse_gen_1_pulse), .clock(CLOCK), .RESET(RESET));
  not not_2 (not_2_out, RESET);
  and and_1 (PC_inc, instruction_register_write, ~s_r_latch_1_qurrent);  // AND_Gate
  equals equals_1 (.in_1(8'h1), .in_2(command), .out_3(equals_1_out_3));
  equals equals_2 (.in_1(8'h2), .in_2(command), .out_3(equals_2_out_3));
  equals equals_3 (.in_1(8'h3), .in_2(command), .out_3(equals_3_out_3));
  equals equals_4 (.in_1(8'h4), .in_2(command), .out_3(equals_4_out_3));
  equals equals_5 (.in_1(8'h5), .in_2(command), .out_3(equals_5_out_3));
  equals equals_6 (.in_1(8'h6), .in_2(command), .out_3(equals_6_out_3));
  equals equals_7 (.in_1(8'h7), .in_2(command), .out_3(equals_7_out_3));
  equals equals_8 (.in_1(8'h8), .in_2(command), .out_3(equals_8_out_3));
  equals equals_9 (.in_1(8'h9), .in_2(command), .out_3(equals_9_out_3));
  equals equals_10 (.in_1(8'ha), .in_2(command), .out_3(equals_10_out_3));
  equals equals_11 (.in_1(8'hb), .in_2(command), .out_3(equals_11_out_3));
  equals equals_12 (.in_1(8'hc), .in_2(command), .out_3(equals_12_out_3));
  equals equals_13 (.in_1(8'hd), .in_2(command), .out_3(equals_13_out_3));
  equals equals_14 (.in_1(8'he), .in_2(command), .out_3(equals_14_out_3));
  equals equals_15 (.in_1(8'hf), .in_2(command), .out_3(equals_15_out_3));
  equals equals_16 (.in_1(8'h10), .in_2(command), .out_3(equals_16_out_3));
  and and_2 (and_2_out, CLOCK, ~PC_disable);  // AND_Gate
  equals equals_17 (.in_1(8'h11), .in_2(command), .out_3(equals_17_out_3));
  equals equals_18 (.in_1(8'h12), .in_2(command), .out_3(equals_18_out_3));
  and and_3 (and_3_out, RESET, ~PC_disable);  // AND_Gate
  equals equals_19 (.in_1(8'h13), .in_2(command), .out_3(equals_19_out_3));
  equals equals_20 (.in_1(8'h14), .in_2(command), .out_3(equals_20_out_3));
  equals equals_21 (.in_1(8'h15), .in_2(command), .out_3(equals_21_out_3));
  equals equals_22 (.in_1(8'h16), .in_2(command), .out_3(equals_22_out_3));
  equals equals_23 (.in_1(8'h17), .in_2(command), .out_3(equals_23_out_3));
  equals equals_24 (.in_1(8'h18), .in_2(command), .out_3(equals_24_out_3));
  equals equals_25 (.in_1(8'h19), .in_2(command), .out_3(equals_25_out_3));
  equals equals_26 (.in_1(8'h1a), .in_2(command), .out_3(equals_26_out_3));
  equals equals_27 (.in_1(8'h1b), .in_2(command), .out_3(equals_27_out_3));
  and and_4 (instruction_register_write, and_2_out, not_3_out);
  not not_3 (not_3_out, f_flipflop_1_qurrent);
  F_flipflop f_flipflop_1 (.flip(CLOCK), .qurrent(f_flipflop_1_qurrent), .RESET(and_3_out));
  AND and_5 (.in_1(equals_1_out_3), .in_2(and_32_out), .out_3(A_to_B));
  AND and_6 (.in_1(equals_2_out_3), .in_2(and_32_out), .out_3(A_to_C));
  AND and_7 (.in_1(equals_3_out_3), .in_2(and_32_out), .out_3(B_to_A));
  AND and_8 (.in_1(equals_4_out_3), .in_2(and_32_out), .out_3(B_to_C));
  AND and_9 (.in_1(equals_5_out_3), .in_2(and_32_out), .out_3(C_to_A));
  AND and_10 (.in_1(equals_6_out_3), .in_2(and_32_out), .out_3(C_to_B));
  AND and_11 (.in_1(equals_7_out_3), .in_2(and_32_out), .out_3(add));
  AND and_12 (.in_1(equals_8_out_3), .in_2(and_32_out), .out_3(ALU_mode));
  AND and_13 (.in_1(equals_9_out_3), .in_2(and_32_out), .out_3(RAM_to_A));
  AND and_14 (.in_1(equals_10_out_3), .in_2(and_32_out), .out_3(RAM_to_B));
  AND and_15 (.in_1(equals_11_out_3), .in_2(and_32_out), .out_3(RAM_to_C));
  AND and_16 (.in_1(equals_12_out_3), .in_2(and_32_out), .out_3(A_to_RAM));
  AND and_17 (.in_1(equals_13_out_3), .in_2(and_32_out), .out_3(B_to_RAM));
  AND and_18 (.in_1(equals_14_out_3), .in_2(and_32_out), .out_3(C_to_RAM));
  AND and_19 (.in_1(equals_15_out_3), .in_2(and_32_out), .out_3(jump));
  AND and_20 (.in_1(equals_16_out_3), .in_2(and_32_out), .out_3(IO_nextByte));
  AND and_21 (.in_1(equals_17_out_3), .in_2(and_32_out), .out_3(IO_readbyte));
  AND and_22 (.in_1(equals_18_out_3), .in_2(and_32_out), .out_3(IO_send));
  AND and_23 (.in_1(equals_19_out_3), .in_2(and_32_out), .out_3(IO_addToArray));
  AND and_24 (.in_1(equals_20_out_3), .in_2(and_32_out), .out_3(IO_getLength));
  AND and_25 (.in_1(equals_21_out_3), .in_2(and_32_out), .out_3(jumpIf));
  AND and_26 (.in_1(equals_22_out_3), .in_2(and_32_out), .out_3(jumpIfNot));
  AND and_27 (.in_1(equals_23_out_3), .in_2(and_32_out), .out_3(ifFlags));
  AND and_28 (.in_1(equals_24_out_3), .in_2(and_32_out), .out_3(ifAvailable));
  AND and_29 (.in_1(equals_25_out_3), .in_2(and_32_out), .out_3(enableToBus));
  AND and_30 (.in_1(equals_26_out_3), .in_2(and_32_out), .out_3(CToIfState));
  AND and_31 (.in_1(equals_27_out_3), .in_2(and_32_out), .out_3(clockhandeler_stop));
  and and_32 (and_32_out, and_2_out, f_flipflop_1_qurrent);
  or or_1 (or_1_out, A_to_B, A_to_C);
  or or_2 (or_2_out, B_to_A, B_to_C);
  or or_3 (or_3_out, C_to_A, C_to_B);
  or or_4 (ALU_enable, add, ALU_mode);
  or or_5 (or_5_out, jump, or_10_out);
  or or_6 (or_6_out, B_to_A, C_to_A);
  or or_7 (or_7_out, A_to_B, C_to_B);
  or or_8 (or_8_out, B_to_C, ALU_enable, A_to_C);
  or or_9 (or_9_out, IO_readbyte, IO_getLength);
  or or_10 (or_10_out, and_34_out, and_33_out);
  and and_33 (and_33_out, if_result_q, jumpIf);
  and and_34 (and_34_out, jumpIfNot, ~if_result_q);  // AND_Gate
  or or_11 (A_read, or_1_out, A_to_RAM);
  or or_12 (B_read, or_2_out, B_to_RAM);
  or or_13 (A_write, or_6_out, RAM_to_A);
  or or_14 (B_write, or_7_out, RAM_to_B);
  or or_15 (C_read, or_3_out, CToIfState, C_to_RAM);
  or or_16 (or_16_out, or_8_out, or_9_out, RAM_to_C);
  or or_17 (or_17_out, RAM_to_C, RAM_to_B, RAM_to_A);
  or or_18 (or_18_out, C_to_RAM, B_to_RAM, A_to_RAM);
  flag_comparer flag_comparer_1 (.flags(ALU_flags), .params(\parameter ), .out(flag_comparer_1_out));
  anyBit anybit_1 (.in_1(BUS), .out_2(anybit_1_out_2));
  and and_35 (and_35_out, anybit_1_out_2, CToIfState);
  and and_36 (and_36_out, flag_comparer_1_out, ifFlags);
  and and_37 (and_37_out, comparator_1_gt, ifAvailable);
  Comparator comparator_1 (.a(\parameter ), .b(IO_length), .gt(comparator_1_gt));  // open: eq, lt
  or or_19 (or_19_out, ifFlags, CToIfState, ifAvailable);
  or or_20 (C_write, or_16_out, enableToBus);
  or or_21 (RAM_read, or_17_out, instruction_register_write);
  or or_22 (RAM_write, or_18_out, inst_loader_1_trigger);
  or or_23 (or_23_out, or_18_out, or_17_out);
  Transistor #(.\type ("n"), .width(8)) transistor_4 (.in(\parameter ), .out(transistor_4_out), .gate(or_23_out));
  Pull_Resistor pull_resistor_1 (.node(transistor_4_out));
  assign RAM_adress = transistor_4_out | transistor_1_out | pull_resistor_2_node;  // OR_Gate or_24, 8 bits wide
  Pull_Resistor pull_resistor_2 (.node(pull_resistor_2_node));
  Transistor #(.\type ("n"), .width(8)) transistor_5 (
    .in(PC_value), .out(pull_resistor_2_node), .gate(instruction_register_write));
  or or_25 (or_25_out, and_3_out, and_32_out);
  Register #(.width(1)) if_result (.D(or_26_out), .en(1'b1), .Q(if_result_q), .clk(and_38_out), .clr(and_3_out));
  or or_26 (or_26_out, and_36_out, and_35_out, and_37_out);
  and and_38 (and_38_out, or_19_out, and_2_out);
  Pull_Resistor pull_resistor_3 (.node(transistor_1_out));
  or or_27 (PC_set, PC_disable, or_5_out);
  assign toBus = {{7{1'b0}}, if_result_q};  // Bit_Extender bit_extender_1
  S_R_latch s_r_latch_1 (.set(PC_set), .reset(or_25_out), .qurrent(s_r_latch_1_qurrent));

  assign IO_toBus = IO_readbyte;
  assign PC_adr = \parameter ;

  // Other names for the same wires on the sheet: BUS__RAMformat_t[15:0] = RAM_data__in; endClock = clockhandeler_stop;
  //   ifStateToC = enableToBus; load = instruction_register_write; loading = PC_disable; params[7:0] = \parameter ;
  //   sub = ALU_mode

  // Notes on the sheet:
  //   IO_send: pull=down
  //   RESET: pull=down
  //   A_write: pull=down
  //   instruction_register_write: pull=down
  //   PC_inc: pull=down
  //   IO_nextByte: pull=down
  //   IO_getLength: pull=down
  //   ALU_flags: pull=down
  //   enableToBus: pull=down
  //   ALU_enable: pull=down
  //   B_read: pull=down
  //   ROM_data: pull=down
  //   IO_addToArray: pull=down
  //   ROM_adress: pull=down
  //   C_write: pull=down
  //   PC_disable: pull=down
  //   IO_readbyte: pull=down
  //   RAM_read: pull=down
  //   A_read: pull=down
  //   RAM_data__in: pull=down
  //   PC_adr: pull=down
  //   ALU_mode: pull=down
  //   parameter: pull=down
  //   IO_toBus: pull=down
  //   RAM_write: pull=down
  //   IO_length: pull=down
  //   PC_value: pull=down
  //   BUS: pull=down
  //   ROM_length: pull=down
  //   PC_set: pull=down
  //   BUS__RAMformat: pull=down
  //   C_read: pull=down
  //   B_write: pull=down
  //   RAM_adress: pull=down
  //   clockhandeler_stop: pull=down
  //   command: pull=down
  //   toBus: pull=down
  //   CLOCK: pull=down
endmodule

module GPIO_co_processor (
  input  in_0,
  input  in_1,
  input  in_2,
  input  in_3,
  input  in_4,
  input  in_5,
  input  in_6,
  input  in_7,
  input  RESET,
  input  refresh,
  input  [7:0] out_pins,
  output out_0,
  output out_1,
  output out_2,
  output out_3,
  output out_4,
  output out_5,
  output out_6,
  output out_7,
  output [7:0] in_pins
);

  data_register in (
    .write(1'b1), .data__in({in_7, in_6, in_5, in_4, in_3, in_2, in_1, in_0}), .RESET(RESET),
    .CLOCK(refresh), .qurrent(in_pins));  // open: read, data__out
  data_register out (
    .write(1'b1), .data__in(out_pins), .RESET(RESET), .CLOCK(refresh),
    .qurrent({out_7, out_6, out_5, out_4, out_3, out_2, out_1, out_0}));  // open: read, data__out

  // Notes on the sheet:
  //   in_7: pull=down
  //   in_5: pull=down
  //   in_pins: pull=down
  //   RESET: pull=down
  //   in_6: pull=down
  //   out_pins: pull=down
  //   out_0: pull=down
  //   out_1: pull=down
  //   in_4: pull=down
  //   refresh: pull=down
  //   out_3: pull=down
  //   out_7: pull=down
  //   in_2: pull=down
  //   out_5: pull=down
  //   in_0: pull=down
  //   in_1: pull=down
  //   in_3: pull=down
  //   out_6: pull=down
  //   out_4: pull=down
  //   out_2: pull=down
endmodule

module pulse_gen (
  input  trigger,
  input  clock,
  input  RESET,
  output pulse
);

  wire register_1_q;

  Register #(.width(1), .trigger("falling")) register_1 (
    .D(trigger), .en(1'b1), .Q(register_1_q), .clk(clock), .clr(RESET));
  and and_1 (pulse, ~register_1_q, clock, trigger);  // AND_Gate

  // Notes on the sheet:
  //   pulse: pull=down
  //   trigger: pull=down
  //   RESET: pull=down
  //   clock: pull=down
endmodule

module T_flipflop (
  input  flip,
  input  RESET,
  output qurrent
);

  wire not_1_out;

  Register #(.width(1)) register_1 (.D(not_1_out), .en(flip), .Q(qurrent), .clk(flip), .clr(RESET));
  not not_1 (not_1_out, qurrent);

  // Notes on the sheet:
  //   flip: pull=down
  //   qurrent: pull=down
  //   RESET: pull=down
endmodule

module AND (
  input  in_1,
  input  in_2,
  output out_3
);

  and and_1 (out_3, in_1, in_2);

  // Notes on the sheet:
  //   in_2: pull=down
  //   out_3: pull=down
  //   in_1: pull=down
endmodule

module PC (
  input  inc,
  input  jump,
  input  [7:0] adr,
  input  clock,
  input  RESET,
  output [7:0] qurrent
);

  Counter #(.trigger("falling")) counter_1 (
    .load(jump), .D(adr), .count(inc), .Q(qurrent), .clk(clock), .clr(RESET));  // open: carry

  // Notes on the sheet:
  //   jump: pull=down
  //   clock: pull=down
  //   inc: pull=down
  //   adr: pull=down
  //   RESET: pull=down
endmodule

module inst_loader (
  input  start,
  input  [7:0] ROM_length,
  input  clock,
  input  RESET,
  output trigger,
  output [7:0] i,
  output done
);

  wire and_1_out, and_2_out, and_3_out, comparator_1_eq, f_flipflop_1_qurrent, not_1_out, not_2_out,
       or_1_out, or_2_out, or_4_out, s_r_latch_1_qurrent;

  or or_1 (or_1_out, start, or_2_out, RESET);
  or or_2 (or_2_out, and_3_out, RESET);
  Comparator comparator_1 (.a(i), .b(ROM_length), .eq(comparator_1_eq));  // open: gt, lt
  not not_1 (not_1_out, comparator_1_eq);
  not not_2 (not_2_out, not_1_out);
  S_R_latch s_r_latch_1 (.set(start), .reset(or_2_out), .qurrent(s_r_latch_1_qurrent));
  not not_3 (done, s_r_latch_1_qurrent);
  counter counter_1 (.INC(and_1_out), .RESET(or_1_out), .Q(i));
  and and_1 (and_1_out, not_1_out, s_r_latch_1_qurrent, clock);
  and and_2 (and_2_out, not_2_out, clock);
  and and_3 (and_3_out, not_2_out, f_flipflop_1_qurrent);
  or or_3 (trigger, and_1_out, and_2_out);
  F_flipflop f_flipflop_1 (.flip(and_2_out), .qurrent(f_flipflop_1_qurrent), .RESET(or_4_out));
  or or_4 (or_4_out, RESET, start);

  // Notes on the sheet:
  //   ROM_length: pull=down
  //   clock: pull=down
  //   trigger: pull=down
  //   RESET: pull=down
  //   done: pull=down
  //   i: pull=down
  //   start: pull=down
endmodule

module inst_RAM (
  input  save,
  input  load,
  input  [7:0] adr,
  input  [15:0] data__in,
  input  clock,
  input  RESET,
  output [15:0] data__out
);

  wire and_1_out, or_1_out;

  or or_1 (or_1_out, load, and_1_out);
  Transistor #(.width(16)) transistor_1 (.in(data__in), .out(data__out), .gate(load));
  and and_1 (and_1_out, save, clock);
  RAM #(.dataWidth(16), .bus("asynch")) ram_1 (.addr(adr), .data(data__out), .sel(or_1_out), .ld(load), .clr(RESET));

  // Notes on the sheet:
  //   load: pull=down
  //   save: pull=down
  //   adr: pull=down
  //   data__in: pull=down
  //   clock: pull=down
  //   RESET: pull=down
  //   data__out: pull=down
endmodule

module S_R_latch (
  input  set,
  input  reset,
  output qurrent
);

  wire nor_1_out;

  nor nor_1 (nor_1_out, set, qurrent);
  nor nor_2 (qurrent, nor_1_out, reset);

  // Notes on the sheet:
  //   set: pull=down
  //   qurrent: pull=down
  //   reset: pull=down
endmodule

module insruction_register (
  input  set,
  input  [15:0] raw_line,
  input  RESET,
  input  CLOCK,
  output [7:0] command,
  output [7:0] \parameter 
);

  Register #(.width(16), .trigger("high")) register_1 (
    .D(raw_line), .en(set), .Q({command, \parameter }), .clk(CLOCK), .clr(RESET));

  // Notes on the sheet:
  //   RESET: pull=down
  //   command: pull=down
  //   parameter: pull=down
  //   CLOCK: pull=down
endmodule

module instruction_splitter (
  input  [15:0] raw,
  output [7:0] command,
  output [7:0] \parameter 
);


  assign command = raw[7:0];
  assign \parameter  = raw[15:8];

  // Notes on the sheet:
  //   parameter: pull=down
  //   raw: pull=down
  //   command: pull=down
endmodule

module instruction_combiner (
  input  [7:0] command,
  input  [7:0] \parameter ,
  output [15:0] combined
);


  assign combined = {\parameter , command};

  // Notes on the sheet:
  //   combined: pull=down
  //   command: pull=down
  //   parameter: pull=down
endmodule

module data_register (
  input  write,
  input  [7:0] data__in,
  input  read,
  input  RESET,
  input  CLOCK,
  output [7:0] qurrent,
  output [7:0] data__out
);

  Register #(.trigger("high")) register_1 (.D(data__in), .en(write), .Q(qurrent), .clk(CLOCK), .clr(RESET));
  Transistor #(.\type ("n"), .width(8)) transistor_1 (.in(qurrent), .out(data__out), .gate(read));

  // Notes on the sheet:
  //   data__out: pull=down
  //   CLOCK: pull=down
  //   data__in: pull=down
  //   write: pull=down
  //   RESET: pull=down
  //   read: pull=down
  //   qurrent: pull=down
endmodule

module ALU (
  input  [7:0] A,
  input  [7:0] B,
  input  adder_mode,
  input  enable,
  output [7:0] math_out,
  output [3:0] flags_out
);

  wire [7:0] adder_1_out, bit_1_and, bit_1_or, subtractor_1_out, transistor_1_out;

  Adder adder_1 (.a(A), .b(B), .out(adder_1_out), .cin(1'b0));  // open: cout
  Transistor #(.width(8)) transistor_1 (.in(adder_1_out), .out(transistor_1_out), .gate(adder_mode));
  Subtractor subtractor_1 (.a(A), .b(B), .out(subtractor_1_out), .bin(1'b0));  // open: bout
  Transistor #(.\type ("n"), .width(8)) transistor_2 (.in(subtractor_1_out), .out(transistor_1_out), .gate(adder_mode));
  Transistor #(.\type ("n"), .width(8)) transistor_3 (.in(transistor_1_out), .out(math_out), .gate(enable));
  Comparator comparator_1 (.a(A), .b(B), .gt(flags_out[0]), .eq(flags_out[1]));  // open: lt
  \bit  bit_1 (.A(A), .B(B), .AND(bit_1_and), .OR(bit_1_or));
  anyBit anybit_1 (.in_1(bit_1_and), .out_2(flags_out[2]));
  anyBit anybit_2 (.in_1(bit_1_or), .out_2(flags_out[3]));

  // Notes on the sheet:
  //   enable: pull=down
  //   adder_mode: pull=down
  //   flags_out: pull=down
  //   math_out: pull=down
  //   B: pull=down
  //   A: pull=down
endmodule

module \bit  (
  input  [7:0] A,
  input  [7:0] B,
  output [7:0] AND,
  output [7:0] OR
);

  assign AND = A & B;  // AND_Gate and_1, 8 bits wide
  assign OR = A | B;  // OR_Gate or_1, 8 bits wide

  // Notes on the sheet:
  //   B: pull=down
  //   OR: pull=down
  //   AND: pull=down
endmodule

module anyBit (
  input  [7:0] in_1,
  output out_2
);

  or or_1 (out_2, in_1[0], in_1[1], in_1[2], in_1[3], in_1[5], in_1[6], in_1[7], in_1[4]);

  // Notes on the sheet:
  //   in_1: pull=down
  //   out_2: pull=down
endmodule

module equals (
  input  [7:0] in_1,
  input  [7:0] in_2,
  output out_3
);

  Comparator comparator_1 (.a(in_1), .b(in_2), .eq(out_3));  // open: gt, lt

  // Notes on the sheet:
  //   in_1: pull=down
  //   out_3: pull=down
  //   in_2: pull=down
endmodule

module IO_module (
  input  [7:0] data_in,
  input  clock_in,
  input  nextByte,
  input  readByte,
  input  send,
  input  addToArray,
  input  [7:0] byteIn,
  input  CLOCK,
  input  RESET,
  input  CLEAR,
  output [7:0] data_out,
  output clock_out,
  output [7:0] out,
  output [7:0] length
);

  wire equals_1_out_3, or_1_out, or_2_out, pulse_gen_1_pulse, register_1_q, s_r_latch_1_qurrent,
       transistor_4_out;
  wire [7:0] counter_1_q, counter_2_q, counter_4_q, transistor_1_out, transistor_5_out;

  Register #(.width(1)) register_1 (.D(send), .en(1'b1), .Q(register_1_q), .clk(CLOCK), .clr(or_2_out));
  pulse_gen pulse_gen_1 (.trigger(register_1_q), .pulse(pulse_gen_1_pulse), .clock(CLOCK), .RESET(or_2_out));
  counter counter_1 (.INC(addToArray), .RESET(or_2_out), .Q(counter_1_q));
  S_R_latch s_r_latch_1 (.set(pulse_gen_1_pulse), .reset(or_1_out), .qurrent(s_r_latch_1_qurrent));
  or or_1 (or_1_out, or_2_out, equals_1_out_3);
  equals equals_1 (.in_1(counter_2_q), .in_2(counter_1_q), .out_3(equals_1_out_3));
  Transistor #(.width(8)) transistor_1 (.in(counter_1_q), .out(transistor_1_out), .gate(s_r_latch_1_qurrent));
  Transistor #(.\type ("n"), .width(8)) transistor_2 (
    .in(counter_2_q), .out(transistor_1_out), .gate(s_r_latch_1_qurrent));
  RAM #(.bus("separate")) ram_1 (
    .addr(transistor_1_out), .din(byteIn), .data(data_out), .str(addToArray), .sel(1'b1), .clk(addToArray),
    .ld(s_r_latch_1_qurrent), .clr(or_2_out));
  counter counter_2 (.INC(clock_out), .RESET(equals_1_out_3), .Q(counter_2_q));
  Transistor #(.\type ("n")) transistor_3 (.in(CLOCK), .out(clock_out), .gate(s_r_latch_1_qurrent));
  or or_2 (or_2_out, RESET, CLEAR);
  Transistor transistor_4 (.in(clock_in), .out(transistor_4_out), .gate(s_r_latch_1_qurrent));
  Pull_Resistor pull_resistor_1 (.node(transistor_4_out));
  counter counter_3 (.INC(transistor_4_out), .RESET(or_2_out), .Q(length));
  counter counter_4 (.INC(nextByte), .RESET(or_2_out), .Q(counter_4_q));
  Transistor #(.width(8)) transistor_5 (.in(length), .out(transistor_5_out), .gate(readByte));
  Transistor #(.\type ("n"), .width(8)) transistor_6 (.in(counter_4_q), .out(transistor_5_out), .gate(readByte));
  RAM #(.bus("separate")) ram_2 (
    .addr(transistor_5_out), .din(data_in), .data(out), .str(transistor_4_out), .sel(1'b1),
    .clk(transistor_4_out), .ld(readByte), .clr(or_2_out));

  // Notes on the sheet:
  //   data_in: pull=down
  //   data_out: pull=down
  //   clock_in: pull=down
  //   CLEAR: pull=down
  //   clock_out: pull=down
  //   addToArray: pull=down
  //   send: pull=down
  //   out: pull=down
  //   RESET: pull=down
  //   CLOCK: pull=down
  //   nextByte: pull=down
  //   length: pull=down
  //   byteIn: pull=down
  //   readByte: pull=down
endmodule

module counter (
  input  INC,
  input  RESET,
  output [7:0] Q
);

  Counter #(.trigger("falling")) counter_1 (.count(1'b1), .Q(Q), .clk(INC), .clr(RESET));  // open: load, D, carry

  // Notes on the sheet:
  //   RESET: pull=down
  //   Q: pull=down
  //   INC: pull=down
endmodule

module flag_comparer (
  input  [3:0] flags,
  input  [7:0] params,
  output out
);

  wire and_1_out, and_2_out, and_3_out, and_4_out, and_5_out, and_6_out, and_7_out, and_8_out, not_1_out,
       not_2_out, not_3_out, not_4_out, not_5_out, not_6_out, not_7_out, not_8_out;

  and and_1 (and_1_out, params[0], flags[0]);
  not not_1 (not_1_out, and_1_out);
  not not_2 (not_2_out, and_2_out);
  and and_2 (and_2_out, params[1], flags[1]);
  not not_3 (not_3_out, and_3_out);
  and and_3 (and_3_out, params[2], flags[2]);
  not not_4 (not_4_out, and_4_out);
  and and_4 (and_4_out, params[3], flags[3]);
  and and_5 (and_5_out, ~flags[0], params[4]);  // AND_Gate
  not not_5 (not_5_out, and_5_out);
  not not_6 (not_6_out, and_6_out);
  and and_6 (and_6_out, ~flags[1], params[5]);  // AND_Gate
  not not_7 (not_7_out, and_7_out);
  and and_7 (and_7_out, ~flags[2], params[6]);  // AND_Gate
  and and_8 (and_8_out, ~flags[3], params[7]);  // AND_Gate
  not not_8 (not_8_out, and_8_out);
  and and_9 (out, not_1_out, not_2_out, not_3_out, not_4_out, not_5_out, not_6_out, not_7_out, not_8_out);

  // Notes on the sheet:
  //   out: pull=down
  //   flags: pull=down
  //   params: pull=down
endmodule

module F_flipflop (
  input  flip,
  input  RESET,
  output qurrent
);

  wire not_1_out;

  Register #(.width(1), .trigger("falling")) register_1 (
    .D(not_1_out), .en(1'b1), .Q(qurrent), .clk(flip), .clr(RESET));
  not not_1 (not_1_out, qurrent);

  // Notes on the sheet:
  //   flip: pull=down
  //   qurrent: pull=down
  //   RESET: pull=down
endmodule

module clock_handeler (
  input  clock_in,
  input  stop,
  input  start,
  output clock_out
);

  wire s_r_latch_1_qurrent;

  and and_1 (clock_out, clock_in, ~s_r_latch_1_qurrent);  // AND_Gate
  S_R_latch s_r_latch_1 (.set(stop), .reset(start), .qurrent(s_r_latch_1_qurrent));

  // Notes on the sheet:
  //   clock_in: pull=down
  //   clock_out: pull=down
  //   stop: pull=down
  //   start: pull=down
endmodule

module logical_for (
  input  start,
  input  [7:0] i_under,
  input  clock,
  input  RESET,
  output trigger,
  output [7:0] i,
  output done
);

  wire comparator_1_lt, not_1_out, or_1_out, or_2_out, s_r_latch_1_qurrent;

  Comparator comparator_1 (.a(i), .b(i_under), .lt(comparator_1_lt));  // open: gt, eq
  S_R_latch s_r_latch_1 (.set(start), .reset(or_2_out), .qurrent(s_r_latch_1_qurrent));
  counter counter_1 (.INC(trigger), .RESET(or_1_out), .Q(i));
  or or_1 (or_1_out, start, or_2_out, RESET);
  or or_2 (or_2_out, not_1_out, RESET);
  not not_1 (not_1_out, comparator_1_lt);
  not not_2 (done, s_r_latch_1_qurrent);
  and and_1 (trigger, comparator_1_lt, s_r_latch_1_qurrent, clock);

  // Notes on the sheet:
  //   done: pull=down
  //   trigger: pull=down
  //   start: pull=down
  //   RESET: pull=down
  //   i: pull=down
  //   clock: pull=down
  //   i_under: pull=down
endmodule

module bitMAN (
  input  enable,
  input  mode,
  input  val,
  input  [7:0] in,
  input  [7:0] bitsel,
  input  CLOCK,
  output [7:0] out
);

  wire and_1_out, and_2_out;
  wire [7:0] bitoverride_1_out, bitselect_1_out, transistor_1_out;
  wire [7:7] anybit_1_out_2;

  bitOverride bitoverride_1 (
    .in(in[0]), .out(bitoverride_1_out[0]), .\this (8'h1), .select(bitsel), .write(and_2_out), .value(val));
  bitOverride bitoverride_2 (
    .in(in[1]), .out(bitoverride_1_out[1]), .\this (8'h2), .select(bitsel), .write(and_2_out), .value(val));
  bitOverride bitoverride_3 (
    .in(in[2]), .out(bitoverride_1_out[2]), .\this (8'h4), .select(bitsel), .write(and_2_out), .value(val));
  bitOverride bitoverride_4 (
    .in(in[3]), .out(bitoverride_1_out[3]), .\this (8'h8), .select(bitsel), .write(and_2_out), .value(val));
  bitOverride bitoverride_5 (
    .in(in[4]), .out(bitoverride_1_out[4]), .\this (8'h10), .select(bitsel), .write(and_2_out), .value(val));
  bitOverride bitoverride_6 (
    .in(in[5]), .out(bitoverride_1_out[5]), .\this (8'h20), .select(bitsel), .write(and_2_out), .value(val));
  bitOverride bitoverride_7 (
    .in(in[6]), .out(bitoverride_1_out[6]), .\this (8'h40), .select(bitsel), .write(and_2_out), .value(val));
  bitOverride bitoverride_8 (
    .in(in[7]), .out(bitoverride_1_out[7]), .\this (8'h80), .select(bitsel), .write(and_2_out), .value(val));
  and and_1 (and_1_out, CLOCK, mode);
  and and_2 (and_2_out, ~mode, CLOCK);  // AND_Gate
  Transistor #(.\type ("n"), .width(8)) transistor_1 (.in(bitoverride_1_out), .out(transistor_1_out), .gate(and_2_out));
  bitSelect bitselect_1 (.in(in[0]), .out(bitselect_1_out[0]), .\this (8'h1), .select(bitsel));
  bitSelect bitselect_2 (.in(in[1]), .out(bitselect_1_out[1]), .\this (8'h2), .select(bitsel));
  bitSelect bitselect_3 (.in(in[2]), .out(bitselect_1_out[2]), .\this (8'h4), .select(bitsel));
  bitSelect bitselect_4 (.in(in[3]), .out(bitselect_1_out[3]), .\this (8'h8), .select(bitsel));
  bitSelect bitselect_5 (.in(in[4]), .out(bitselect_1_out[4]), .\this (8'h10), .select(bitsel));
  Transistor #(.\type ("n"), .gate("br"), .width(8)) transistor_2 (
    .in({8{anybit_1_out_2[7]}}), .out(transistor_1_out), .gate(and_1_out));
  bitSelect bitselect_6 (.in(in[5]), .out(bitselect_1_out[5]), .\this (8'h20), .select(bitsel));
  bitSelect bitselect_7 (.in(in[6]), .out(bitselect_1_out[6]), .\this (8'h40), .select(bitsel));
  anyBit anybit_1 (.in_1(bitselect_1_out), .out_2(anybit_1_out_2[7]));
  bitSelect bitselect_8 (.in(in[7]), .out(bitselect_1_out[7]), .\this (8'h80), .select(bitsel));
  Transistor #(.\type ("n"), .width(8)) transistor_3 (.in(transistor_1_out), .out(out), .gate(enable));

  // Notes on the sheet:
  //   mode: pull=down
  //   bitsel: pull=down
  //   CLOCK: pull=down
  //   out: pull=down
  //   val: pull=down
  //   in: pull=down
endmodule

module bitOverride (
  input  in,
  input  [7:0] \this ,
  input  [7:0] select,
  input  write,
  input  value,
  output out
);

  wire and_2_out, anybit_1_out_2;
  wire [7:0] and_1_out;

  anyBit anybit_1 (.in_1(and_1_out), .out_2(anybit_1_out_2));
  assign and_1_out = \this  & select;  // AND_Gate and_1, 8 bits wide
  and and_2 (and_2_out, anybit_1_out_2, write);
  Transistor transistor_1 (.in(in), .out(out), .gate(and_2_out));
  Transistor #(.\type ("n")) transistor_2 (.in(value), .out(out), .gate(and_2_out));

  // Notes on the sheet:
  //   write: pull=down
  //   this: pull=down
  //   out: pull=down
  //   value: pull=down
  //   select: pull=down
  //   in: pull=down
endmodule

module bitSelect (
  input  in,
  input  [7:0] \this ,
  input  [7:0] select,
  output out
);

  wire anybit_1_out_2;
  wire [7:0] and_1_out;

  anyBit anybit_1 (.in_1(and_1_out), .out_2(anybit_1_out_2));
  assign and_1_out = \this  & select;  // AND_Gate and_1, 8 bits wide
  Pull_Resistor pull_resistor_1 (.node(out));
  Transistor #(.\type ("n"), .gate("br")) transistor_1 (.in(in), .out(out), .gate(anybit_1_out_2));

  // Notes on the sheet:
  //   this: pull=down
  //   select: pull=down
  //   out: pull=down
endmodule
